// Logisim project cpu.circ as structural Verilog: 1 circuit, main circuit main
module main (
  input  [31:0] INSTRUCTION,
  input  CLOCK,
  output [31:0] PROGRAM_COUNTER,
  output [31:0] ra,
  output [31:0] sp,
  output [31:0] t0,
  output [31:0] t1,
  output [31:0] t2,
  output [31:0] s0,
  output [31:0] s1,
  output [31:0] a0
);

  wire BSel, RegWEn;
  wire [2:0] ImmSel;
  wire [3:0] ALUSel;
  wire [31:0] adder_1_out, EX_STAGE, IF_STAGE, Imm, multiplexer_1_out, rs1, rs2;

  control_logic control_logic_1 (
    .BSel(BSel), .RegWEn(RegWEn), .ImmSel(ImmSel), .inst(IF_STAGE), .ALUSel(ALUSel));  // open: BrUn, ASel, PCSel, BrLt, BrEq, MemRW, WBSel
  Adder #(.width(32)) adder_1 (.a(PROGRAM_COUNTER), .b(32'h4), .out(adder_1_out));  // open: cin, cout
  Register #(.width(32)) PC (.D(adder_1_out), .clk(CLOCK), .Q(PROGRAM_COUNTER));  // open: en, clr
  // branch_comp branch_comp_1: pin names not known
  Register #(.width(32)) register_1 (.D(INSTRUCTION), .clk(CLOCK), .Q(IF_STAGE));  // open: en, clr
  imm_gen imm_gen_1 (.ImmSel(ImmSel), .inst(IF_STAGE), .imm(Imm));
  regfile_main RegFile (
    .rs2(IF_STAGE[24:20]), .rd(IF_STAGE[11:7]), .Read_Data_1(rs1), .Read_Data_2(rs2), .ra(ra), .sp(sp),
    .t0(t0), .t1(t1), .t2(t2), .s0(s0), .s1(s1), .a0(a0), .rs1(IF_STAGE[19:15]), .Write_Data(EX_STAGE),
    .RegWEn(RegWEn), .clk(CLOCK));
  Multiplexer #(.width(32), .enable("false")) multiplexer_1 (.in0(rs2), .in1(Imm), .out(multiplexer_1_out), .sel(BSel));
  alu Arithmetic_Logic_Unit (.Result(EX_STAGE), .ALUSel(ALUSel), .A(rs1), .B(multiplexer_1_out));
  // mem_main DMEM: pin names not known; wires that end beside it: CLOCK

  // Other names for the same wires on the sheet: clk = CLOCK

  // Notes on the sheet:
  //   Output
  //   IMEM (do **NOT** move this)
  //   Inputs
  //   Inputs/Outputs for testing. Do **NOT** move these.
endmodule
